// Logisim project 4to1mux.circ as structural Verilog: 1 circuit, main circuit main
module main (
  input  I0,
  input  I1,
  input  I2,
  input  I3,
  input  S1,
  input  S0,
  output Y
);

  wire nS0, nS1, T0, T1, T2, T3;

  not not_1 (nS1, S1);
  not not_2 (nS0, S0);
  and and_1 (T0, I0, nS1, nS0);
  and and_2 (T1, I1, nS1, S0);
  and and_3 (T2, I2, S1, nS0);
  and and_4 (T3, I3, S1, S0);
  or or_1 (Y, T1, T2);

  // Notes on the sheet:
  //   4-to-1 Multiplexer
endmodule
